// Logisim project control.circ as structural Verilog: 1 circuit, main circuit control_main
module control_main (
  input  Finished,
  input  Product_0,
  input  Clock,
  output Load_Product,
  output Load_M,
  output Select_Add,
  output Select_Product,
  output Counter_Increment,
  output Counter_Reset,
  output Load_Result
);

  wire and_1_out, and_2_out, and_3_out, and_4_out, and_5_out, and_6_out, and_7_out, s5_out, xor_1_out;
  wire [2:0] n0_out, register_1_q;

  Register #(.width(3)) register_1 (.D(n0_out), .en(1'b1), .Q(register_1_q), .clk(Clock));  // open: clr
  and and_1 (and_1_out, ~register_1_q[2], register_1_q[1], register_1_q[0]);  // AND_Gate
  and and_2 (and_2_out, register_1_q[2], ~register_1_q[1]);  // AND_Gate
  or n2 (n0_out[2], and_1_out, and_2_out);
  xor xor_1 (xor_1_out, register_1_q[0], register_1_q[1]);
  and and_3 (and_3_out, xor_1_out, ~register_1_q[2]);  // AND_Gate
  and and_4 (and_4_out, register_1_q[2], register_1_q[1], ~register_1_q[0], ~Finished);  // AND_Gate
  or n1 (n0_out[1], and_3_out, and_2_out, and_4_out);
  and and_5 (and_5_out, ~register_1_q[2], ~register_1_q[0]);  // AND_Gate
  and and_6 (and_6_out, ~register_1_q[2], register_1_q[1], register_1_q[0], ~Product_0);  // AND_Gate
  and and_7 (and_7_out, register_1_q[2], register_1_q[1], ~register_1_q[0], ~Finished);  // AND_Gate
  or n0 (n0_out[0], and_5_out, and_6_out, and_7_out);
  and s1 (Counter_Reset, ~register_1_q[2], ~register_1_q[1], register_1_q[0]);  // AND_Gate
  and s2 (Select_Product, ~register_1_q[2], register_1_q[1], ~register_1_q[0]);  // AND_Gate
  and s4 (Select_Add, register_1_q[2], ~register_1_q[1], ~register_1_q[0]);  // AND_Gate
  and s5 (s5_out, register_1_q[2], ~register_1_q[1], register_1_q[0]);  // AND_Gate
  and s6 (Counter_Increment, register_1_q[2], register_1_q[1], ~register_1_q[0]);  // AND_Gate
  or or_1 (Load_Product, Select_Product, Select_Add, s5_out);
  and and_8 (Load_Result, Counter_Increment, Finished);

  assign Load_M = Counter_Reset;
endmodule
