// Logisim project datapath.circ as structural Verilog: 4 circuits, main circuit datapath_main
module datapath_main (
  input  [31:0] Multiplicand,
  input  [31:0] Multiplier,
  input  Load_M,
  input  Select_Product,
  input  Counter_Increment,
  input  Load_Product,
  input  Counter_Reset,
  input  Select_Add,
  input  Clock,
  input  Load_Result,
  output Product_0,
  output [31:0] Result_Left,
  output [31:0] Result_Right,
  output Finished
);

  wire n32bitadder_1_cout;
  wire [31:0] multiplexer_1_out, multiplexer_2_out, multiplexer_3_out, n32bitadder_1_result, Product_Left_q,
       register_1_q, register_2_q, shifter_1_output_left, shifter_1_output_right;
  wire [31:1] Product_Right_q;

  Multiplexer #(.width(32), .enable("false")) multiplexer_1 (
    .in0(shifter_1_output_left), .in1({32{1'b0}}), .out(multiplexer_1_out), .sel(Select_Product));
  Multiplexer #(.width(32), .enable("false")) multiplexer_2 (
    .in0(shifter_1_output_right), .in1(register_2_q), .out(multiplexer_2_out), .sel(Select_Product));
  Register #(.width(32)) register_1 (.D(Multiplicand), .en(Load_M), .Q(register_1_q), .clk(Clock));  // open: clr
  Register #(.width(32)) register_2 (.D(Multiplier), .en(Load_M), .Q(register_2_q), .clk(Clock));  // open: clr
  Register #(.width(32)) Product_Left (
    .D(multiplexer_1_out), .en(Load_Product), .Q(Product_Left_q), .clk(Clock));  // open: clr
  Register #(.width(32)) Product_Right (
    .D(multiplexer_2_out), .en(Load_Product), .Q({Product_Right_q, Product_0}), .clk(Clock));  // open: clr
  _32BitAdder u_32bitadder_1 (
    .Cout(n32bitadder_1_cout), .A(Product_Left_q), .B(register_1_q), .Result(n32bitadder_1_result), .Cin(1'b0));
  shifter shifter_1 (
    .input_right({Product_Right_q, Product_0}), .input_left(multiplexer_3_out),
    .input_bit(n32bitadder_1_cout), .output_right(shifter_1_output_right), .output_left(shifter_1_output_left));
  Multiplexer #(.width(32), .enable("false")) multiplexer_3 (
    .in0(Product_Left_q), .in1(n32bitadder_1_result), .out(multiplexer_3_out), .sel(Select_Add));
  Counter #(.width(5), .max('h1f)) counter_1 (
    .count(Counter_Increment), .carry(Finished), .clk(Clock), .clr(Counter_Reset));  // open: load, D, Q
  Register #(.width(32)) register_3 (.D(Product_Left_q), .en(Load_Result), .Q(Result_Left), .clk(Clock));  // open: clr
  Register #(.width(32)) register_4 (
    .D({Product_Right_q, Product_0}), .en(Load_Result), .Q(Result_Right), .clk(Clock));  // open: clr

  // Notes on the sheet:
  //   32 Bit Adder
  //   Shifter
endmodule

module shifter (
  input  [31:0] input_right,
  input  [31:0] input_left,
  input  input_bit,
  output [31:0] output_right,
  output [31:0] output_left
);


  assign output_left = {input_bit, input_left[31:1]};
  assign output_right = {input_left[0], input_right[31:1]};
endmodule

module _1BitAdder (
  input  A,
  input  B,
  input  Cin,
  output S,
  output Cout
);

  wire and_1_out, and_2_out, xor_1_out;

  xor xor_1 (xor_1_out, A, B);
  xor xor_2 (S, xor_1_out, Cin);
  and and_1 (and_1_out, xor_1_out, Cin);
  and and_2 (and_2_out, A, B);
  or or_1 (Cout, and_1_out, and_2_out);
endmodule

module _32BitAdder (
  input  [31:0] A,
  input  [31:0] B,
  input  Cin,
  output [31:0] Result,
  output Cout
);

  wire S0_cout, S1_cout, S2_cout, S3_cout, S4_cout, S5_cout, S6_cout, S7_cout, S8_cout, S9_cout, S10_cout,
       S11_cout, S12_cout, S13_cout, S14_cout, S15_cout, S16_cout, S17_cout, S18_cout, S19_cout, S20_cout,
       S21_cout, S22_cout, S23_cout, S24_cout, S25_cout, S26_cout, S27_cout, S28_cout, S29_cout, S30_cout;

  _1BitAdder S15 (.A(A[15]), .B(B[15]), .Cin(S14_cout), .S(Result[15]), .Cout(S15_cout));
  _1BitAdder S16 (.A(B[16]), .B(A[16]), .Cin(S15_cout), .S(Result[16]), .Cout(S16_cout));
  _1BitAdder S14 (.A(A[14]), .B(B[14]), .Cin(S13_cout), .S(Result[14]), .Cout(S14_cout));
  _1BitAdder S17 (.A(B[17]), .B(A[17]), .Cin(S16_cout), .S(Result[17]), .Cout(S17_cout));
  _1BitAdder S13 (.A(A[13]), .B(B[13]), .Cin(S12_cout), .S(Result[13]), .Cout(S13_cout));
  _1BitAdder S18 (.A(B[18]), .B(A[18]), .Cin(S17_cout), .S(Result[18]), .Cout(S18_cout));
  _1BitAdder S12 (.A(A[12]), .B(B[12]), .Cin(S11_cout), .S(Result[12]), .Cout(S12_cout));
  _1BitAdder S19 (.A(B[19]), .B(A[19]), .Cin(S18_cout), .S(Result[19]), .Cout(S19_cout));
  _1BitAdder S11 (.A(A[11]), .B(B[11]), .Cin(S10_cout), .S(Result[11]), .Cout(S11_cout));
  _1BitAdder S20 (.A(B[20]), .B(A[20]), .Cin(S19_cout), .S(Result[20]), .Cout(S20_cout));
  _1BitAdder S10 (.A(A[10]), .B(B[10]), .Cin(S9_cout), .S(Result[10]), .Cout(S10_cout));
  _1BitAdder S21 (.A(B[21]), .B(A[21]), .Cin(S20_cout), .S(Result[21]), .Cout(S21_cout));
  _1BitAdder S9 (.A(A[9]), .B(B[9]), .Cin(S8_cout), .S(Result[9]), .Cout(S9_cout));
  _1BitAdder S22 (.A(B[22]), .B(A[22]), .Cin(S21_cout), .S(Result[22]), .Cout(S22_cout));
  _1BitAdder S8 (.A(A[8]), .B(B[8]), .Cin(S7_cout), .S(Result[8]), .Cout(S8_cout));
  _1BitAdder S23 (.A(B[23]), .B(A[23]), .Cin(S22_cout), .S(Result[23]), .Cout(S23_cout));
  _1BitAdder S7 (.A(A[7]), .B(B[7]), .Cin(S6_cout), .S(Result[7]), .Cout(S7_cout));
  _1BitAdder S24 (.A(B[24]), .B(A[24]), .Cin(S23_cout), .S(Result[24]), .Cout(S24_cout));
  _1BitAdder S6 (.A(A[6]), .B(B[6]), .Cin(S5_cout), .S(Result[6]), .Cout(S6_cout));
  _1BitAdder S25 (.A(B[25]), .B(A[25]), .Cin(S24_cout), .S(Result[25]), .Cout(S25_cout));
  _1BitAdder S5 (.A(A[5]), .B(B[5]), .Cin(S4_cout), .S(Result[5]), .Cout(S5_cout));
  _1BitAdder S26 (.A(B[26]), .B(A[26]), .Cin(S25_cout), .S(Result[26]), .Cout(S26_cout));
  _1BitAdder S4 (.A(A[4]), .B(B[4]), .Cin(S3_cout), .S(Result[4]), .Cout(S4_cout));
  _1BitAdder S27 (.A(B[27]), .B(A[27]), .Cin(S26_cout), .S(Result[27]), .Cout(S27_cout));
  _1BitAdder S3 (.A(A[3]), .B(B[3]), .Cin(S2_cout), .S(Result[3]), .Cout(S3_cout));
  _1BitAdder S28 (.A(B[28]), .B(A[28]), .Cin(S27_cout), .S(Result[28]), .Cout(S28_cout));
  _1BitAdder S2 (.A(A[2]), .B(B[2]), .Cin(S1_cout), .S(Result[2]), .Cout(S2_cout));
  _1BitAdder S29 (.A(B[29]), .B(A[29]), .Cin(S28_cout), .S(Result[29]), .Cout(S29_cout));
  _1BitAdder S1 (.A(A[1]), .B(B[1]), .Cin(S0_cout), .S(Result[1]), .Cout(S1_cout));
  _1BitAdder S30 (.A(B[30]), .B(A[30]), .Cin(S29_cout), .S(Result[30]), .Cout(S30_cout));
  _1BitAdder S0 (.A(A[0]), .B(B[0]), .Cin(Cin), .S(Result[0]), .Cout(S0_cout));
  _1BitAdder S31 (.A(B[31]), .B(A[31]), .Cin(S30_cout), .S(Result[31]), .Cout(Cout));
endmodule
