// Logisim project mult32.circ as structural Verilog: 1 circuit, main circuit main
module main (
  input  [31:0] Multiplicand,
  input  [31:0] Multiplier,
  output [31:0] Most_Significant_32_Bit,
  output [31:0] Less_Significant_32_Bit
);

  wire clock_1_out, control_main_1_counter_increment, control_main_1_counter_reset, control_main_1_load_m,
       control_main_1_load_product, control_main_1_load_result, control_main_1_select_add,
       control_main_1_select_product, datapath_main_1_finished, datapath_main_1_product_0;

  Clock clock_1 (.out(clock_1_out));
  datapath_main datapath_main_1 (
    .Multiplicand(Multiplicand), .Multiplier(Multiplier), .Load_M(control_main_1_load_m),
    .Select_Product(control_main_1_select_product), .Counter_Increment(control_main_1_counter_increment),
    .Load_Product(control_main_1_load_product), .Counter_Reset(control_main_1_counter_reset),
    .Select_Add(control_main_1_select_add), .Clock(clock_1_out), .Load_Result(control_main_1_load_result),
    .Product_0(datapath_main_1_product_0), .Result_Left(Most_Significant_32_Bit),
    .Result_Right(Less_Significant_32_Bit), .Finished(datapath_main_1_finished));
  control_main control_main_1 (
    .Finished(datapath_main_1_finished), .Product_0(datapath_main_1_product_0), .Clock(clock_1_out),
    .Load_Product(control_main_1_load_product), .Load_M(control_main_1_load_m),
    .Select_Add(control_main_1_select_add), .Select_Product(control_main_1_select_product),
    .Counter_Increment(control_main_1_counter_increment), .Counter_Reset(control_main_1_counter_reset),
    .Load_Result(control_main_1_load_result));

  // Notes on the sheet:
  //   Constants for examples
endmodule
